// Logisim project cpuProject.circ as structural Verilog: 4 circuits, main circuit main
module main (
);

  wire clock_1_out;
  wire [7:0] ram_1_data;

  ALU alu_1 ();  // open: Input_A, Result, Input_B, OP_code
  // AND_Gate and_1 is placed but not wired
  // NOT_Gate not_1 is placed but not wired
  Clock clock_1 (.out(clock_1_out));
  RAM ram_1 (.addr(ram_1_data), .data(ram_1_data), .clk(clock_1_out));  // open: sel, ld, clr
endmodule

module ALU (
  input  [7:0] Input_A,
  input  [7:0] Input_B,
  input  [2:0] OP_code,
  output [7:0] Result
);

  wire [7:0] adder_1_out, divider_1_out, multiplier_1_out, negator_1_out, subtractor_1_out;

  Adder adder_1 (.a(Input_A), .b(Input_B), .out(adder_1_out));  // open: cin, cout
  Subtractor subtractor_1 (.a(Input_A), .b(Input_B), .out(subtractor_1_out));  // open: bin, bout
  Multiplier multiplier_1 (.a(Input_A), .b(Input_B), .out(multiplier_1_out));  // open: cin, cout
  Divider divider_1 (.a(Input_A), .b(Input_B), .out(divider_1_out));  // open: upper, rem
  Negator negator_1 (.in(Input_A), .out(negator_1_out));
  Multiplexer #(.select(3), .width(8), .enable("false")) multiplexer_1 (
    .in0(adder_1_out), .in1(subtractor_1_out), .in2(multiplier_1_out), .in3(divider_1_out),
    .in4(negator_1_out), .out(Result), .sel(OP_code));  // open: in5, in6, in7

  // Other names for the same wires on the sheet: ALU[7:0] = Result

  // Notes on the sheet:
  //   ALU
endmodule

module Decoder (
);


  // Notes on the sheet:
  //   move
  //   copy
  //   delete
  //   add
  //   subtract
  //   multiply
  //   divide
  //   invert
  //   Decoder
endmodule

module Registers (
);

  Register R1 ();  // open: D, en, Q, clk, clr
  Register R2 ();  // open: D, en, Q, clk, clr
endmodule
